# Fritzing sketch Breath project (saved by Fritzing 0.9.3b)
breadboards: 1

parts:
  M1 = DOIT Esp32 DevKit v1 (30 pins long, 11 pins width) [part_number=ESP32S-PIN30]
  M2 = BMP280
  Componente1 = Adafruit SCD4x [part_number="Adafruit #5187"]
  IC1 = 2.8 inch LCD SPI display with touch screen & SD card
  A1 = ZP07 air quality detection module
  A2 = PMS5003  # not connected

nets:
  3V3: M1.3V3, M2.VIN, Componente1.3.3V
  GND: M1.GND, M2.GND, Componente1.GND, A1.Pin_4
  N1: M1.D15, IC1.pin_12
  N2: M1.D2, IC1.pin_10
  N3: M1.D4, IC1.pin_11
  N4: M1.RX2, A1.Pin_1
  N5: M1.TX2, A1.Pin_2
  N6: M1.D5, IC1.pin4
  N7: M1.D18, IC1.pin5, IC1.pin8
  N8: M1.D19, IC1.pin2, IC1.pin6
  N9: M1.D21, M2.SDA, Componente1.SDA
  N10: M1.D22, M2.SCL, Componente1.SCL
  N11: M1.D23, IC1.pin3, IC1.pin_9
  N12: M1.D27, IC1.pin1
  N13: M1.VIN, A1.Pin_3
  N14: IC1.pin7, IC1.pin_14

custom parts:
  DOIT Esp32 DevKit v1 (30 pins long, 11 pins width): The DOIT Esp32 DevKit v1 is one of the development board created by DOIT to evaluate the ESP-WROOM-32 module. It is based on the ESP32 microcontroller that boasts Wifi, Bluetooth, Ethernet and Low Power support all in a single chip. (vanepp) made breadboard work, adjusted pin numbering and labels and reduced size of schematic and cleaned up pcb. This chip is 30pins long (2 x15) and 11 pins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
  BMP280: Temperature Humidity Barometric presure Sensor, I2C
  Adafruit SCD4x: Take a deep breath in...now slowly breathe out. Mmm isn't it wonderful? All that air around us, which we bring into our lungs, extracts oxygen from and then breathes out carbon dioxide. CO2 is essential for life on this planet we call Earth - we and plants take turns using and emitting CO2 in an elegant symbiosis. But it's important to keep that CO2 balanced - you don't want too much around,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
  2.8 inch LCD SPI display with touch screen & SD card: A generic 2.8 inch LCD TFT 320x280 display with touchscreen and SD card slot.
  ZP07 air quality detection module: ZP07 air-quality module adopts flat surface semiconductor gas sensor. The module has good sensitivity to volatile organic gases such as formaldehyde, benzene, carbon monoxide, ammonia, hydrogen, alcohol and smoke of cigarette, essence etc.
  PMS5003: PMS5003 is a kind of digital and universal particle concentration sensor, which can be used to obtain the number of suspended particles in the air.
